# Fritzing sketch Smarte (saved by Fritzing 0.9.3b)
breadboards: 2

parts:
  Componente1 = Arduino Uno (Rev3)
  U1 = ESP8266 WiFi Module [part_number=ESP8266]
  hc-sr1 = hc-sr04
  KY-1 = Keyes Relay [package=THT]
  DHT11_1 = DHT11 module
  FC-1 = Sound Sensor
  SERVOAzucar = Tower Pro SG90 servo [part_number=101246]
  SERVO2 = Tower Pro SG90 servo [part_number=101246]
  R1 = Resistor [tolerance=±5% resistance=220 package="0603 [SMD]"]
  R2 = Resistor [tolerance=±5% resistance=220 package="0603 [SMD]"]
  LEDPWM = LED - 3mm [color="Red (633nm)" package="3 mm [THT]"]
  LEDTermometro = LED - 3mm [color="Red (633nm)" package="3 mm [THT]"]

nets:
  N1: Componente1.A0, DHT11_1.DATA
  N2: Componente1.A1, FC-1.OUT
  N3: Componente1.D8, KY-1.signal
  GND: Componente1.D9_PWM, Componente1.GND, U1.GND, hc-sr1.Echo, hc-sr1.GND, KY-1.ground, DHT11_1.GND, FC-1.GND, SERVOAzucar.GND, SERVO2.GND
  N4: Componente1.D10_PWM/SS, hc-sr1.Trig
  N5: Componente1.D11_PWM/MOSI, SERVO2.Signal
  N6: Componente1.D12/MISO, SERVOAzucar.Signal
  N7: Componente1.D2, U1.TXD
  N8: Componente1.D3_PWM, U1.RXD
  N9: Componente1.D4, R2.Pin_0
  N10: Componente1.D5_PWM, R1.Pin_0
  3V3: Componente1.3V3, U1.VCC, U1.CH_PD
  VCC: Componente1.5V, DHT11_1.VCC, FC-1.VCC
  +5V: hc-sr1.VCC, SERVOAzucar.+5V, SERVO2.+5V
  N11: R1.Pin_1, LEDPWM.anode
  N12: R2.Pin_1, LEDTermometro.anode

custom parts:
  ESP8266 WiFi Module: Generic WiFi Module based on the ESP8266 with onboard PCB antenna and UART communications
  Keyes Relay: The Keyes 5V relay module is suitable for SCM development, home appliance control. It uses a 5V~12V TIL control signal which can control DC / AC signal.
  DHT11 module: DHT11 black pcb module
  Tower Pro SG90 servo: Original file by John De Cristofaro http://www.adafruit.com/products/1449 Adafruit Feedback Servo (Small) Edited by: e-radionica.com 28/9/2015
